// Digital circuit SOP.dig as structural Verilog
module SOP (
  input  A,
  input  B,
  input  C,
  input  D,
  output Y
);

  wire and_1_out, and_2_out, and_3_out, and_4_out, and_5_out, and_6_out, and_7_out, not_1_out, not_2_out,
       not_3_out, not_4_out, or_1_out, or_3_out;

  not not_1 (not_1_out, A);
  not not_2 (not_2_out, B);
  not not_3 (not_3_out, C);
  not not_4 (not_4_out, D);
  and and_1 (and_1_out, not_1_out, not_2_out, not_3_out, D);
  and and_2 (and_2_out, not_1_out, not_2_out, C, D);
  and and_3 (and_3_out, not_1_out, B, not_3_out, D);
  and and_4 (and_4_out, not_1_out, B, C, D);
  and and_5 (and_5_out, A, not_2_out, not_3_out, not_4_out);
  and and_6 (and_6_out, A, not_2_out, C, not_4_out);
  and and_7 (and_7_out, A, B, not_3_out, not_4_out);
  or or_1 (or_1_out, and_4_out, and_3_out, and_2_out, and_1_out);
  or or_2 (Y, or_3_out, or_1_out);
  or or_3 (or_3_out, and_7_out, and_6_out, and_5_out);

  // Notes on the sheet:
  //   A: MSB
  //   D: LSB
  //   Use A as the most-significant bit and 
  //   D as the least-significant bit.
endmodule

/* Test case:
A B C D Y
0 0 0 0 X
0 0 0 1 1
0 0 1 0 0
0 0 1 1 1 
0 1 0 0 0 
0 1 0 1 1 
0 1 1 0 0
0 1 1 1 1 
1 0 0 0 1
1 0 0 1 0
1 0 1 0 1
1 0 1 1 0 
1 1 0 0 1 
1 1 0 1 X
1 1 1 0 X
1 1 1 1 X
*/
