// Digital circuit test.dig as structural Verilog
module test (
  input  D,
  input  A,
  output Y
);

  _74151 _74151_1 (
    .pin1(1'b0), .pin2(1'b0), .pin3(1'b1), .pin4(1'b1), .pin5(Y), .pin7(1'b0), .pin8(1'b0), .pin9(A),
    .pin10(D), .pin11(1'b0), .pin12(1'b0), .pin13(1'b1), .pin14(1'b0), .pin15(1'b1), .pin16(1'b1));  // open: pin6
endmodule
